# Fritzing sketch PotBoard SKETCH (saved by Fritzing 0.9.3b)
breadboards: 1

parts:
  Parça1 = Arduino Uno (Rev3)
  R1 = Resistor [tolerance=±5% resistance=10k package="2010 [SMD]"]
  R2 = Resistor [tolerance=±5% resistance=220 package="2010 [SMD]"]
  R3 = Trimmer Potentiometer [maximum_resistance=10kΩ package=THT]
  R4 = Trimmer Potentiometer [maximum_resistance=10kΩ package=THT]
  S3 = Round Pushbutton
  S4 = Round Pushbutton
  LCD1 = LCD screen
  R5 = Resistor [tolerance=±5% resistance=10k package="0603 [SMD]"]
  R6 = Resistor [tolerance=±5% resistance=220 package="0603 [SMD]"]
  LED1 = LED - 3mm [color="Red (633nm)" package="3 mm [THT]"]
  LED2 = LED - 3mm [color="Red (633nm)" package="3 mm [THT]"]
  SG1 = Buzzer 12mm [package=buzzer-12mm-ns]

nets:
  N1: Parça1.A0, R3.wiper
  N2: Parça1.A1, R4.wiper
  N3: Parça1.A2, R1.Pin_0, S4.leg0
  N4: Parça1.A3, S3.leg0, R5.Pin_0
  N5: Parça1.D9_PWM, LED1.cathode
  N6: Parça1.D11_PWM/MOSI, LCD1.E
  N7: Parça1.D12/MISO, LCD1.RS
  N8: Parça1.D2, LCD1.DB7
  N9: Parça1.D3_PWM, LCD1.DB6
  N10: Parça1.D4, LCD1.DB5
  N11: Parça1.D5_PWM, LCD1.DB4
  N12: Parça1.D6_PWM, LED2.cathode, SG1.2
  5V: Parça1.5V, R1.Pin_1, R3.leg2, R4.leg2, LCD1.VDD, LCD1.LED+, R5.Pin_1
  GND: Parça1.GND, R2.Pin_1, R3.leg1, R4.leg1, S3.leg1, S4.leg1, LCD1.VSS, LCD1.R/W, LCD1.LED-, R6.Pin_1
  N13: R2.Pin_0, LED2.anode
  N14: R6.Pin_0, LED1.anode

notes:
  PotBoard Project by Emre Cebeci
  https://github.com/emreyigitcbc/PotBoard
